// Logisim project Lab05_counter.circ as structural Verilog: 7 circuits, main circuit main
module main (
  input  Reset,
  output [3:0] out_2
);

  wire clk_out;

  Clock clk (.out(clk_out));
  Clock sysclc ();  // open: out
  Up_counter up_counter_1 (.clk(clk_out), .rst(Reset), .Up(out_2));
  Hex_Digit_Display hex_digit_display_1 (.value(out_2));  // open: dp
endmodule

module Up_counter (
  input  clk,
  input  rst,
  output [3:0] Up
);

  wire d_ff_1_qn, d_ff_2_qn, d_ff_3_qn, d_ff_4_qn;

  D_Flip_Flop d_ff_1 (.D(d_ff_1_qn), .clk(clk), .Q(Up[0]), .Qn(d_ff_1_qn), .reset(rst));  // open: preset
  D_Flip_Flop d_ff_2 (.D(d_ff_2_qn), .clk(d_ff_1_qn), .Q(Up[1]), .Qn(d_ff_2_qn), .reset(rst));  // open: preset
  D_Flip_Flop d_ff_3 (.D(d_ff_3_qn), .clk(d_ff_2_qn), .Q(Up[2]), .Qn(d_ff_3_qn), .reset(rst));  // open: preset
  D_Flip_Flop d_ff_4 (.D(d_ff_4_qn), .clk(d_ff_3_qn), .Q(Up[3]), .Qn(d_ff_4_qn), .reset(rst));  // open: preset
endmodule

module Down_counter (
  input  clk,
  input  rst,
  output [3:0] Down
);

  wire d_ff_1_qn, d_ff_2_qn, d_ff_3_qn, d_ff_4_qn;

  D_Flip_Flop d_ff_1 (.D(d_ff_1_qn), .clk(clk), .Q(Down[0]), .Qn(d_ff_1_qn), .preset(rst));  // open: reset
  D_Flip_Flop d_ff_2 (.D(d_ff_2_qn), .clk(Down[0]), .Q(Down[1]), .Qn(d_ff_2_qn), .preset(rst));  // open: reset
  D_Flip_Flop d_ff_3 (.D(d_ff_3_qn), .clk(Down[1]), .Q(Down[2]), .Qn(d_ff_3_qn), .preset(rst));  // open: reset
  D_Flip_Flop d_ff_4 (.D(d_ff_4_qn), .clk(Down[2]), .Q(Down[3]), .Qn(d_ff_4_qn), .preset(rst));  // open: reset
endmodule

module Johnson_counter (
  input  clk,
  input  rst,
  output [3:0] Johnson
);

  wire d_ff_4_qn;

  D_Flip_Flop d_ff_1 (.D(d_ff_4_qn), .clk(clk), .Q(Johnson[0]), .preset(rst));  // open: Qn, reset
  D_Flip_Flop d_ff_2 (.D(Johnson[0]), .clk(clk), .Q(Johnson[1]), .reset(rst));  // open: Qn, preset
  D_Flip_Flop d_ff_3 (.D(Johnson[1]), .clk(clk), .Q(Johnson[2]), .reset(rst));  // open: Qn, preset
  D_Flip_Flop d_ff_4 (.D(Johnson[2]), .clk(clk), .Q(Johnson[3]), .Qn(d_ff_4_qn), .reset(rst));  // open: preset
endmodule

module Universal (
  input  [2:0] Sel
);

  wire decade_counter_1_p1, down_counter_1_p1, johnson_counter_1_p1, ring_counter_1_p1, up_counter_1_p1;

  // Up_counter up_counter_1: pin names not known; wires that end beside it: up_counter_1_p1
  // Down_counter down_counter_1: pin names not known; wires that end beside it: down_counter_1_p1
  // Johnson_counter johnson_counter_1: pin names not known; wires that end beside it: johnson_counter_1_p1
  // Decade_counter decade_counter_1: pin names not known; wires that end beside it: decade_counter_1_p1
  // Ring_counter ring_counter_1: pin names not known; wires that end beside it: ring_counter_1_p1
  Multiplexer #(.select(3)) multiplexer_1 (
    .in2(up_counter_1_p1), .in3(down_counter_1_p1), .in4(johnson_counter_1_p1), .in5(decade_counter_1_p1),
    .in6(ring_counter_1_p1), .sel(Sel));  // open: in0, in1, in7, out
endmodule

module Decade_counter (
  input  clk,
  input  rst,
  output [3:0] Decade
);

  wire and_1_out, d_ff_1_qn, d_ff_2_qn, d_ff_3_qn, d_ff_4_qn, or_1_out;

  D_Flip_Flop d_ff_1 (.D(d_ff_1_qn), .clk(clk), .Q(Decade[0]), .Qn(d_ff_1_qn), .reset(or_1_out));  // open: preset
  or or_1 (or_1_out, rst, and_1_out);
  D_Flip_Flop d_ff_2 (.D(d_ff_2_qn), .clk(d_ff_1_qn), .Q(Decade[1]), .Qn(d_ff_2_qn), .reset(or_1_out));  // open: preset
  D_Flip_Flop d_ff_3 (.D(d_ff_3_qn), .clk(d_ff_2_qn), .Q(Decade[2]), .Qn(d_ff_3_qn), .reset(or_1_out));  // open: preset
  D_Flip_Flop d_ff_4 (.D(d_ff_4_qn), .clk(d_ff_3_qn), .Q(Decade[3]), .Qn(d_ff_4_qn), .reset(or_1_out));  // open: preset
  and and_1 (and_1_out, Decade[3], Decade[1]);
endmodule

module Ring_counter (
  input  clk,
  input  rst,
  output [3:0] Ring
);

  D_Flip_Flop d_ff_1 (.D(Ring[3]), .clk(clk), .Q(Ring[0]), .preset(rst));  // open: Qn, reset
  D_Flip_Flop d_ff_2 (.D(Ring[0]), .clk(clk), .Q(Ring[1]), .reset(rst));  // open: Qn, preset
  D_Flip_Flop d_ff_3 (.D(Ring[1]), .clk(clk), .Q(Ring[2]), .reset(rst));  // open: Qn, preset
  D_Flip_Flop d_ff_4 (.D(Ring[2]), .clk(clk), .Q(Ring[3]), .reset(rst));  // open: Qn, preset
endmodule
